// Logisim project TugasMandiri_4.circ as structural Verilog: 8 circuits, main circuit Soal_1a_Lama
module Soal_1a_Horizontal (
  input  I0,
  input  I1,
  input  I2,
  input  I3,
  output O0,
  output O1,
  output O2,
  output O3,
  output O4,
  output O5,
  output O6,
  output O7,
  output O8,
  output O9,
  output O10,
  output O11,
  output O12,
  output O13,
  output O14,
  output O15
);

  wire decoder_1_out0, decoder_1_out1, decoder_1_out2, decoder_1_out3, decoder_2_out0, decoder_2_out1,
       decoder_2_out2, decoder_2_out3;

  Decoder #(.enable("false"), .select(2)) decoder_1 (
    .out0(decoder_1_out0), .out1(decoder_1_out1), .out2(decoder_1_out2), .out3(decoder_1_out3), .sel({I0, I1}));
  Decoder #(.enable("false"), .select(2)) decoder_2 (
    .out0(decoder_2_out0), .out1(decoder_2_out1), .out2(decoder_2_out2), .out3(decoder_2_out3), .sel({I2, I3}));
  and and_1 (O0, decoder_1_out0, decoder_2_out0);
  and and_2 (O1, decoder_1_out1, decoder_2_out0);
  and and_3 (O2, decoder_1_out2, decoder_2_out0);
  and and_4 (O3, decoder_1_out3, decoder_2_out0);
  and and_5 (O4, decoder_1_out0, decoder_2_out1);
  and and_6 (O5, decoder_1_out1, decoder_2_out1);
  and and_7 (O6, decoder_1_out2, decoder_2_out1);
  and and_8 (O7, decoder_1_out3, decoder_2_out1);
  and and_9 (O8, decoder_1_out0, decoder_2_out2);
  and and_10 (O9, decoder_1_out1, decoder_2_out2);
  and and_11 (O10, decoder_1_out2, decoder_2_out2);
  and and_12 (O11, decoder_1_out3, decoder_2_out2);
  and and_13 (O12, decoder_1_out0, decoder_2_out3);
  and and_14 (O13, decoder_1_out1, decoder_2_out3);
  and and_15 (O14, decoder_1_out2, decoder_2_out3);
  and and_16 (O15, decoder_1_out3, decoder_2_out3);

  // Notes on the sheet:
  //   Input
  //   Output
endmodule

module Soal_1a_Vertical (
  input  I0,
  input  I1,
  input  I2,
  input  I3,
  output O0,
  output O1,
  output O2,
  output O3,
  output O4,
  output O5,
  output O6,
  output O7,
  output O8,
  output O9,
  output O10,
  output O11,
  output O12,
  output O13,
  output O14,
  output O15
);

  wire decoder_1_out0, decoder_1_out1, decoder_1_out2, decoder_1_out3, decoder_2_out0, decoder_2_out1,
       decoder_2_out2, decoder_2_out3;

  Decoder #(.enable("false"), .select(2)) decoder_1 (
    .out0(decoder_1_out0), .out1(decoder_1_out1), .out2(decoder_1_out2), .out3(decoder_1_out3), .sel({I1, I0}));
  Decoder #(.enable("false"), .select(2)) decoder_2 (
    .out0(decoder_2_out0), .out1(decoder_2_out1), .out2(decoder_2_out2), .out3(decoder_2_out3), .sel({I3, I2}));
  and and_1 (O0, decoder_1_out0, decoder_2_out0);
  and and_2 (O1, decoder_1_out1, decoder_2_out0);
  and and_3 (O2, decoder_1_out2, decoder_2_out0);
  and and_4 (O3, decoder_1_out3, decoder_2_out0);
  and and_5 (O4, decoder_1_out0, decoder_2_out1);
  and and_6 (O5, decoder_1_out1, decoder_2_out1);
  and and_7 (O6, decoder_1_out2, decoder_2_out1);
  and and_8 (O7, decoder_1_out3, decoder_2_out1);
  and and_9 (O8, decoder_1_out0, decoder_2_out2);
  and and_10 (O9, decoder_1_out1, decoder_2_out2);
  and and_11 (O10, decoder_1_out2, decoder_2_out2);
  and and_12 (O11, decoder_1_out3, decoder_2_out2);
  and and_13 (O12, decoder_1_out0, decoder_2_out3);
  and and_14 (O13, decoder_1_out1, decoder_2_out3);
  and and_15 (O14, decoder_1_out2, decoder_2_out3);
  and and_16 (O15, decoder_1_out3, decoder_2_out3);

  // Notes on the sheet:
  //   Input
  //   Output
endmodule

module Soal_1a_Lama (
  input  I0,
  input  I1,
  input  I2,
  input  I3,
  output O0,
  output O1,
  output O2,
  output O3,
  output O4,
  output O5,
  output O6,
  output O7,
  output O8,
  output O9,
  output O10,
  output O11,
  output O12,
  output O13,
  output O14,
  output O15
);

  wire and_1_out, and_2_out, and_3_out, and_4_out, and_5_out, and_6_out, and_7_out, and_8_out, not_1_out,
       not_2_out, not_3_out, not_4_out;

  not not_1 (not_1_out, I0);
  not not_2 (not_2_out, I1);
  not not_3 (not_3_out, I2);
  not not_4 (not_4_out, I3);
  and and_1 (and_1_out, not_1_out, not_2_out);
  and and_2 (and_2_out, I0, not_2_out);
  and and_3 (and_3_out, not_1_out, I1);
  and and_4 (and_4_out, I0, I1);
  and and_5 (and_5_out, not_3_out, not_4_out);
  and and_6 (and_6_out, I2, not_4_out);
  and and_7 (and_7_out, not_3_out, I3);
  and and_8 (and_8_out, I2, I3);
  and and_9 (O0, and_1_out, and_5_out);
  and and_10 (O1, and_2_out, and_5_out);
  and and_11 (O2, and_3_out, and_5_out);
  and and_12 (O3, and_4_out, and_5_out);
  and and_13 (O4, and_1_out, and_6_out);
  and and_14 (O5, and_2_out, and_6_out);
  and and_15 (O6, and_3_out, and_6_out);
  and and_16 (O7, and_4_out, and_6_out);
  and and_17 (O8, and_1_out, and_7_out);
  and and_18 (O9, and_2_out, and_7_out);
  and and_19 (O10, and_3_out, and_7_out);
  and and_20 (O11, and_4_out, and_7_out);
  and and_21 (O12, and_1_out, and_8_out);
  and and_22 (O13, and_2_out, and_8_out);
  and and_23 (O14, and_3_out, and_8_out);
  and and_24 (O15, and_4_out, and_8_out);

  // Notes on the sheet:
  //   Input
  //   Output
endmodule

module Soal_1b (
  input  S0,
  input  S1,
  input  S2,
  input  EN,
  input  I0,
  input  I1,
  input  I2,
  input  I3,
  input  I4,
  input  I5,
  input  I6,
  input  I7,
  output O
);

  wire and_1_out, and_2_out, and_3_out, and_4_out, and_5_out, and_6_out, and_7_out, and_8_out, and_9_out,
       not_1_out, not_2_out, not_3_out, not_4_out, not_5_out, not_6_out, not_7_out, not_8_out, not_9_out,
       not_10_out, not_11_out, not_12_out;

  not not_1 (not_1_out, S0);
  not not_2 (not_2_out, S2);
  not not_3 (not_3_out, S1);
  and and_1 (and_1_out, not_1_out, not_3_out, not_2_out, I0);
  and and_2 (and_2_out, S0, not_3_out, not_2_out, I1);
  and and_3 (and_3_out, not_1_out, S1, not_2_out, I2);
  and and_4 (and_4_out, S0, S1, not_2_out, I3);
  and and_5 (and_5_out, not_1_out, not_3_out, S2, I4);
  and and_6 (and_6_out, S0, not_3_out, S2, I5);
  and and_7 (and_7_out, not_1_out, S1, S2, I6);
  and and_8 (and_8_out, S0, S1, S2, I7);
  not not_4 (not_4_out, and_1_out);
  not not_5 (not_5_out, and_2_out);
  not not_6 (not_6_out, and_3_out);
  not not_7 (not_7_out, and_4_out);
  not not_8 (not_8_out, and_5_out);
  not not_9 (not_9_out, and_6_out);
  not not_10 (not_10_out, and_7_out);
  not not_11 (not_11_out, and_8_out);
  and and_9 (and_9_out, not_4_out, not_5_out, not_6_out, not_7_out, not_8_out, not_9_out, not_10_out, not_11_out);
  not not_12 (not_12_out, and_9_out);
  and and_10 (O, EN, not_12_out);

  // Notes on the sheet:
  //   Selector
  //   Index Selector
  //   Enabler
  //   Output
endmodule

module Soal_2a (
  input  A,
  input  B,
  input  C,
  input  D,
  output W,
  output X,
  output Y,
  output Z
);

  Multiplexer #(.select(2)) multiplexer_1 (.in0(1'b0), .in1(1'b1), .in2(1'b1), .in3(1'b0), .out(X), .sel({A, B}));
  Multiplexer #(.select(2)) multiplexer_2 (.in0(1'b0), .in1(1'b1), .in2(1'b1), .in3(1'b0), .out(Y), .sel({B, C}));
  Multiplexer #(.select(2)) multiplexer_3 (.in0(1'b0), .in1(1'b1), .in2(1'b1), .in3(1'b0), .out(Z), .sel({C, D}));

  assign W = A;

  // Notes on the sheet:
  //   Input (Binary Code)
  //   Output (Gray Code)
endmodule

module Soal_2b (
  input  A,
  input  B,
  input  C,
  input  D,
  output X,
  output Y,
  output Z
);

  wire and_1_out, and_2_out, multiplexer_3_out, multiplexer_4_out, not_1_out;

  Multiplexer #(.select(2)) multiplexer_1 (.in0(1'b1), .in1(1'b0), .in2(1'b0), .in3(1'b1), .out(X), .sel({B, C}));
  Multiplexer #(.select(2)) multiplexer_2 (.in0(1'b0), .in1(1'b1), .in2(1'b0), .in3(1'b0), .out(Y), .sel({B, C}));
  Multiplexer #(.select(2)) multiplexer_3 (
    .in0(1'b0), .in1(1'b1), .in2(1'b1), .in3(1'b0), .out(multiplexer_3_out), .sel({B, D}));
  not not_1 (not_1_out, A);
  Multiplexer #(.select(2)) multiplexer_4 (
    .in0(1'b1), .in1(1'b0), .in2(1'b0), .in3(1'b1), .out(multiplexer_4_out), .sel({B, D}));
  and and_1 (and_1_out, A, multiplexer_3_out);
  and and_2 (and_2_out, not_1_out, multiplexer_4_out);
  or or_1 (Z, and_1_out, and_2_out);

  // Notes on the sheet:
  //   Input (Binary Code)
  //   Output (Gray Code)
endmodule

module Soal_3a (
  input  A,
  input  B,
  input  C,
  input  D,
  output F
);

  wire and_1_out, and_2_out, not_1_out, not_2_out, not_3_out, or_1_out;

  not not_1 (not_1_out, C);
  or or_1 (or_1_out, not_1_out, not_2_out);
  not not_2 (not_2_out, D);
  not not_3 (not_3_out, D);
  and and_1 (and_1_out, B, or_1_out);
  and and_2 (and_2_out, C, A, not_3_out);
  or or_2 (F, and_1_out, and_2_out);
endmodule

module Soal_3b (
  input  A,
  input  B,
  input  C,
  input  D,
  output F
);

  wire and_1_out, and_2_out, not_1_out, not_2_out, not_3_out;

  and and_1 (and_1_out, A, B);
  not not_1 (not_1_out, C);
  not not_2 (not_2_out, A);
  and and_2 (and_2_out, not_1_out, not_2_out, not_3_out);
  not not_3 (not_3_out, B);
  or or_1 (F, and_1_out, and_2_out);
endmodule
